# Fritzing sketch ATTiny Temp Display (saved by Fritzing 1.0.4)
circuit board: 5.8cm x 4cm
breadboards: 1

parts:
  TMP = LM35 Temperature Sensor [package="TO92 [THT]"]
  SWITCH = Pushbutton [package="[THT]"]
  R1 = Resistor [tolerance=±5% power=0.25W resistance=10k package=THT]
  OLED = OLED 128x64 I2C Monochrome Display VDD-GND
  J1 = female pin header, 2 pins [form="♀ (female)"]
  ATTINY85 = attiny85 [package=dip]

nets:
  N1: TMP.+Vs, ATTINY85.Pin_6
  N2: TMP.Vout, ATTINY85.Pin_3
  GND: TMP.GND, R1.Pin_0, OLED.GND, J1.pin1, ATTINY85.Pin_4
  N3: SWITCH.Pin_1, SWITCH.Pin_2, R1.Pin_1, ATTINY85.Pin_2
  N4: SWITCH.Pin_3, SWITCH.Pin_4, OLED.VDD, J1.pin2, ATTINY85.Pin_8
  N5: OLED.SCK, ATTINY85.Pin_7
  N6: OLED.SDA, ATTINY85.Pin_5

notes:
  ATTINY85 Temp v1.0

custom parts:
  OLED 128x64 I2C Monochrome Display VDD-GND: OLED 128x64 I2C Monochrome Display. Note: there are two variants of this part, this one is the VDD GND SCK SDA variant. The other is GND VDD SCK SDA. Make sure you select the part that matches your module as using the incorrect part will probably destroy your module! In addition the mounting holes are marked on silkscreen but not by default drilled. If you want drilled mounting holes, copy a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
